# Fritzing sketch arduino-pong (saved by Fritzing 0.9.3b)
breadboards: 1

parts:
  Part1 = Arduino Uno (Rev3)
  R1 = Rotary Potentiometer (Small) [maximum_resistance=100kΩ package=THT]
  S1 = Pushbutton [package="[THT]"]
  LED1 = LED - 5mm [color="Green (555nm)" package="5 mm [THT]"]
  LED2 = LED - 5mm [color="Red (633nm)" package="5 mm [THT]"]
  R2 = Resistor [tolerance=±5% resistance=220 package=THT]
  R3 = Resistor [tolerance=±5% resistance=220 package=THT]
  R4 = Resistor [tolerance=±5% resistance=10k package=THT]

nets:
  N1: Part1.A2, R1.wiper
  N2: Part1.D8, LED1.anode
  N3: Part1.D11_PWM/MOSI, S1.Pin_3, S1.Pin_4, R4.Pin_1
  N4: Part1.D7, LED2.anode
  N5: R1.leg1, S1.Pin_1, S1.Pin_2
  N6: R1.leg2, R2.Pin_0, R3.Pin_0, R4.Pin_0
  N7: LED1.cathode, R2.Pin_1
  N8: LED2.cathode, R3.Pin_1
